// Logisim project alu.circ as structural Verilog: 4 circuits, main circuit full_adder_4bits_carry_lkhd
module full_adder_4bits_carry_lkhd (
  input  [3:0] opcode,
  input  minus,
  input  [7:0] a,
  input  [7:0] b,
  output [7:0] out_5,
  output overflow
);

  wire and_1_out, and_2_out, and_3_out, and_4_out, and_5_out, and_6_out, and_7_out, and_8_out, and_10_out,
       and_11_out, and_12_out, and_13_out, and_14_out, and_15_out, and_16_out, and_17_out, and_18_out,
       and_19_out, and_20_out, and_21_out, and_22_out, and_23_out, and_24_out, and_25_out, and_26_out,
       and_27_out, and_28_out, and_29_out, and_30_out, not_1_out, not_2_out, not_3_out, not_4_out, or_2_out,
       or_3_out, or_4_out, or_5_out, or_6_out, or_7_out, or_8_out, or_10_out, xor_1_out, xor_2_out,
       xor_3_out, xor_4_out, xor_5_out, xor_6_out, xor_7_out, xor_8_out, xor_9_out, xor_10_out, xor_11_out,
       xor_16_out, xor_18_out, xor_20_out, xor_22_out, xor_23_out;

  not not_1 (not_1_out, opcode[0]);
  not not_2 (not_2_out, opcode[1]);
  not not_3 (not_3_out, opcode[2]);
  not not_4 (not_4_out, opcode[3]);
  // AND_Gate ADD has open pins: in0=not_4_out, in1=not_3_out, in2=not_2_out, in3=not_1_out, out=open
  // AND_Gate ADC has open pins: in0=not_4_out, in1=not_3_out, in2=not_2_out, in3=opcode[0], out=open
  // AND_Gate SUB has open pins: in0=not_4_out, in1=not_3_out, in2=opcode[1], in3=not_1_out, out=open
  xor xor_1 (xor_1_out, b[0], minus);
  xor xor_2 (xor_2_out, b[1], minus);
  xor xor_3 (xor_3_out, b[2], minus);
  // AND_Gate SBB has open pins: in0=not_4_out, in1=not_3_out, in2=opcode[1], in3=opcode[0], out=open
  xor xor_4 (xor_4_out, a[0], xor_1_out);
  and and_1 (and_1_out, xor_1_out, a[0]);
  xor xor_5 (xor_5_out, a[1], xor_2_out);
  and and_2 (and_2_out, xor_2_out, a[1]);
  xor xor_6 (xor_6_out, a[2], xor_3_out);
  and and_3 (and_3_out, xor_3_out, a[2]);
  xor xor_7 (xor_7_out, b[3], minus);
  and and_4 (and_4_out, xor_7_out, a[3]);
  xor xor_8 (xor_8_out, b[4], minus);
  and and_5 (and_5_out, xor_8_out, a[4]);
  xor xor_9 (xor_9_out, b[5], minus);
  and and_6 (and_6_out, xor_9_out, a[5]);
  xor xor_10 (xor_10_out, b[6], minus);
  and and_7 (and_7_out, xor_10_out, a[6]);
  xor xor_11 (xor_11_out, b[7], minus);
  // AND_Gate ONC has open pins: in0=not_4_out, in1=opcode[2], in2=not_2_out, in3=not_1_out, out=open
  xor xor_12 (out_5[0], minus, xor_4_out);
  xor xor_13 (out_5[1], or_2_out, xor_5_out);
  xor xor_14 (out_5[2], or_3_out, xor_6_out);
  xor xor_15 (out_5[3], or_4_out, xor_16_out);
  xor xor_16 (xor_16_out, a[3], xor_7_out);
  xor xor_17 (out_5[4], or_10_out, xor_18_out);
  xor xor_18 (xor_18_out, a[4], xor_8_out);
  xor xor_19 (out_5[5], or_6_out, xor_20_out);
  xor xor_20 (xor_20_out, a[5], xor_9_out);
  xor xor_21 (out_5[6], or_7_out, xor_22_out);
  xor xor_22 (xor_22_out, a[6], xor_10_out);
  xor xor_23 (xor_23_out, a[7], xor_11_out);
  and and_8 (and_8_out, xor_11_out, a[7]);
  // AND_Gate TWC has open pins: in0=not_4_out, in1=opcode[2], in2=not_2_out, in3=opcode[0], out=open
  xor xor_24 (out_5[7], or_8_out, xor_23_out);
  // AND_Gate AND_9 has open pins: in0=not_4_out, in1=opcode[2], in2=opcode[1], in3=not_1_out, out=open
  and and_10 (and_10_out, minus, xor_4_out);
  and and_11 (and_11_out, minus, xor_4_out, xor_5_out);
  and and_12 (and_12_out, and_1_out, xor_5_out);
  and and_13 (and_13_out, minus, xor_4_out, xor_5_out, xor_6_out);
  and and_14 (and_14_out, and_1_out, xor_5_out, xor_6_out);
  and and_15 (and_15_out, and_2_out, xor_6_out);
  and and_16 (and_16_out, minus, xor_4_out, xor_5_out, xor_6_out, xor_16_out);
  and and_17 (and_17_out, and_1_out, xor_5_out, xor_6_out, xor_16_out);
  and and_18 (and_18_out, and_2_out, xor_6_out, xor_16_out);
  and and_19 (and_19_out, and_3_out, xor_16_out);
  and and_20 (and_20_out, or_10_out, xor_18_out);
  and and_21 (and_21_out, or_10_out, xor_18_out, xor_20_out);
  and and_22 (and_22_out, and_5_out, xor_20_out);
  and and_23 (and_23_out, or_10_out, xor_18_out, xor_20_out, xor_22_out);
  and and_24 (and_24_out, and_5_out, xor_20_out, xor_22_out);
  and and_25 (and_25_out, and_6_out, xor_22_out);
  and and_26 (and_26_out, or_10_out, xor_18_out, xor_20_out, xor_22_out, xor_23_out);
  and and_27 (and_27_out, and_5_out, xor_20_out, xor_22_out, xor_23_out);
  and and_28 (and_28_out, and_6_out, xor_22_out, xor_23_out);
  and and_29 (and_29_out, and_7_out, xor_23_out);
  // AND_Gate OR has open pins: in0=not_4_out, in1=opcode[2], in2=opcode[1], in3=opcode[0], out=open
  // AND_Gate XOR_25 has open pins: in0=opcode[3], in1=not_3_out, in2=not_2_out, in3=not_1_out, out=open
  or or_2 (or_2_out, and_10_out, and_1_out);
  or or_3 (or_3_out, and_11_out, and_12_out, and_2_out);
  or or_4 (or_4_out, and_13_out, and_14_out, and_15_out, and_3_out);
  or or_5 (or_5_out, and_16_out, and_17_out, and_18_out, and_19_out, and_4_out);
  or or_6 (or_6_out, and_20_out, and_5_out);
  or or_7 (or_7_out, and_21_out, and_22_out, and_6_out);
  or or_8 (or_8_out, and_23_out, and_24_out, and_25_out, and_7_out);
  or or_9 (overflow, and_26_out, and_27_out, and_28_out, and_29_out, and_8_out);
  // AND_Gate LSL has open pins: in0=opcode[3], in1=not_3_out, in2=not_2_out, in3=opcode[0], out=open
  or or_10 (or_10_out, and_16_out, and_30_out);
  and and_30 (and_30_out, minus, or_5_out);
  // AND_Gate LSR has open pins: in0=opcode[3], in1=not_3_out, in2=opcode[1], in3=not_1_out, out=open
  // AND_Gate ASR has open pins: in0=opcode[3], in1=not_3_out, in2=opcode[1], in3=opcode[0], out=open
  // AND_Gate ROL has open pins: in0=opcode[3], in1=opcode[2], in2=not_2_out, in3=not_1_out, out=open
  // AND_Gate ROR has open pins: in0=opcode[3], in1=opcode[2], in2=not_2_out, in3=opcode[0], out=open
  // AND_Gate RCL has open pins: in0=opcode[3], in1=opcode[2], in2=opcode[1], in3=not_1_out, out=open
  // AND_Gate RCR has open pins: in0=opcode[3], in1=opcode[2], in2=opcode[1], in3=opcode[0], out=open
endmodule

module chameleon (
  input  a,
  input  b,
  input  x1,
  input  x2,
  input  inv_sortie,
  input  no_shift,
  input  shift_left,
  input  shift_right,
  input  in,
  input  c2,
  input  c1,
  input  c0,
  output out,
  output out_2,
  output c2_prime,
  output c1_prime,
  output c0_prime
);

  wire and_1_out, and_2_out, and_3_out, and_4_out, and_5_out, and_6_out, and_7_out, and_8_out, and_9_out,
       and_10_out, nor_1_out;

  and and_1 (and_1_out, a, x1, b);
  nor nor_1 (nor_1_out, b, x2, a);
  and and_2 (and_2_out, no_shift, c0);
  and and_3 (and_3_out, shift_left, c2);
  and and_4 (and_4_out, shift_right, c1);
  and and_5 (and_5_out, no_shift, c1);
  and and_6 (and_6_out, shift_left, c0);
  and and_7 (and_7_out, shift_right, c2);
  and and_8 (and_8_out, no_shift, c2);
  and and_9 (and_9_out, shift_left, c1);
  and and_10 (and_10_out, shift_right, c0);
  or or_1 (c0_prime, and_2_out, and_3_out, and_4_out);
  or or_2 (c1_prime, and_5_out, and_6_out, and_7_out);
  or or_3 (c2_prime, and_8_out, and_9_out, and_10_out);
  nor nor_2 (out, and_1_out, nor_1_out);
  xor xor_1 (out_2, inv_sortie, in);
endmodule

module alu_8bit (
  input  [3:0] opcode,
  input  op,
  input  input_enable,
  input  clock,
  input  C_in,
  input  [7:0] b,
  output shift_left,
  output shift_right,
  output out_9,
  output out_10,
  output out_11,
  output out_12,
  output out_13,
  output out_14,
  output zero,
  output out_16,
  output out_17,
  output carry,
  output \négatif ,
  output overflow
);

  wire ADC_out, ADD_out, and_1_out, and_2_out, and_3_out, AND_4_out, and_5_out, and_6_out, and_7_out,
       and_8_out, and_9_out, and_10_out, and_11_out, and_12_out, and_13_out, and_14_out, and_15_out,
       and_16_out, and_17_out, and_18_out, and_19_out, and_20_out, and_21_out, and_22_out, and_23_out,
       and_24_out, and_25_out, and_26_out, and_27_out, and_28_out, and_29_out, and_30_out, and_31_out,
       and_32_out, and_33_out, and_34_out, and_35_out, and_36_out, and_37_out, and_38_out, and_39_out,
       and_40_out, and_41_out, and_42_out, and_43_out, and_44_out, and_45_out, and_46_out, and_47_out,
       and_48_out, and_49_out, and_50_out, and_51_out, and_52_out, and_53_out, and_54_out, and_55_out,
       and_56_out, and_57_out, and_58_out, and_59_out, and_60_out, and_61_out, and_62_out, and_63_out,
       and_64_out, and_65_out, and_66_out, and_67_out, and_68_out, and_69_out, and_70_out, and_71_out,
       and_72_out, and_73_out, and_74_out, and_75_out, and_76_out, and_77_out, and_78_out, and_79_out,
       and_80_out, and_81_out, and_82_out, and_83_out, ASR_out, CE_out, EA_out, HC_out, IB_out, LC_out,
       LSL_out, LSR_out, nand_1_out, nand_2_out, nand_3_out, nand_4_out, nand_5_out, nand_6_out, nand_7_out,
       nand_8_out, nor_1_out, nor_2_out, nor_3_out, nor_4_out, nor_5_out, nor_6_out, nor_7_out, nor_8_out,
       nor_9_out, nor_10_out, nor_11_out, nor_12_out, nor_13_out, nor_14_out, nor_15_out, nor_16_out,
       nor_18_out, nor_19_out, nor_20_out, nor_21_out, nor_22_out, nor_23_out, nor_24_out, nor_25_out,
       nor_26_out, nor_27_out, nor_28_out, nor_29_out, nor_30_out, nor_31_out, nor_32_out, nor_33_out,
       nor_34_out, nor_35_out, nor_36_out, nor_37_out, nor_38_out, nor_39_out, nor_40_out, nor_41_out,
       nor_42_out, nor_43_out, nor_44_out, nor_45_out, nor_46_out, nor_47_out, nor_48_out, nor_49_out,
       nor_50_out, nor_51_out, nor_52_out, nor_53_out, nor_54_out, nor_55_out, nor_56_out, nor_57_out,
       nor_58_out, nor_60_out, nor_62_out, nor_64_out, nor_66_out, nor_68_out, nor_70_out, nor_72_out,
       not_1_out, not_2_out, not_3_out, not_4_out, not_5_out, NS_out, ONC_out, or_1_out, or_2_out, OR_3_out,
       or_4_out, or_5_out, or_6_out, or_7_out, or_8_out, or_9_out, or_10_out, or_11_out, or_12_out,
       or_13_out, or_14_out, or_15_out, or_16_out, or_17_out, or_18_out, RCL_out, RCR_out, ROL_out, ROR_out,
       SBB_out, SUB_out, TWC_out, x1_out, xnor_1_out, xnor_2_out, xnor_3_out, xnor_4_out, xnor_5_out,
       xnor_6_out, xnor_7_out, xnor_8_out, xor_2_out, xor_3_out, xor_4_out, xor_5_out, xor_6_out, xor_7_out,
       xor_8_out, xor_9_out, XOR_out;

  or CE (CE_out, ADC_out, SBB_out, RCL_out, RCR_out);
  and and_1 (and_1_out, CE_out, C_in);
  not not_1 (not_1_out, opcode[0]);
  not not_2 (not_2_out, opcode[1]);
  not not_3 (not_3_out, opcode[2]);
  not not_4 (not_4_out, opcode[3]);
  or or_1 (or_1_out, ASR_out, ROL_out);
  or LC (LC_out, SBB_out, ROR_out);
  and and_2 (and_2_out, or_1_out, b[7]);
  and and_3 (and_3_out, LC_out, b[0]);
  or or_2 (or_2_out, and_1_out, and_3_out, and_2_out, HC_out);
  and ADD (ADD_out, not_4_out, not_3_out, op, not_2_out, not_1_out);
  or HC (HC_out, XOR_out, TWC_out, SUB_out, AND_4_out);
  and ADC (ADC_out, not_4_out, not_3_out, op, not_2_out, opcode[0]);
  or EA (EA_out, ADD_out, ADC_out, SUB_out, SBB_out, AND_4_out, OR_3_out, XOR_out);
  and SUB (SUB_out, not_4_out, not_3_out, op, opcode[1], not_1_out);
  and SBB (SBB_out, not_4_out, not_3_out, op, opcode[1], opcode[0]);
  or IB (IB_out, SUB_out, SBB_out, XOR_out, ONC_out, TWC_out);
  and ONC (ONC_out, not_4_out, opcode[2], op, not_2_out, not_1_out);
  or x1 (x1_out, ADD_out, XOR_out, ADC_out, SUB_out, ~op, SBB_out, TWC_out, ONC_out, OR_3_out);  // OR_Gate
  and TWC (TWC_out, not_4_out, opcode[2], op, not_2_out, opcode[0]);
  and AND_4 (AND_4_out, not_4_out, opcode[2], op, opcode[1], not_1_out);
  nand nand_1 (nand_1_out, out_10, EA_out);
  nand nand_2 (nand_2_out, out_11, EA_out);
  nand nand_3 (nand_3_out, out_12, EA_out);
  nand nand_4 (nand_4_out, out_13, EA_out);
  nand nand_5 (nand_5_out, out_14, EA_out);
  nand nand_6 (nand_6_out, out_16, EA_out);
  nand nand_7 (nand_7_out, out_17, EA_out);
  and OR_3 (OR_3_out, not_4_out, opcode[2], op, opcode[1], opcode[0]);
  nand nand_8 (nand_8_out, out_9, EA_out);
  xnor xnor_1 (xnor_1_out, b[0], IB_out);
  xnor xnor_2 (xnor_2_out, b[1], IB_out);
  xnor xnor_3 (xnor_3_out, b[2], IB_out);
  xnor xnor_4 (xnor_4_out, b[3], IB_out);
  xnor xnor_5 (xnor_5_out, b[4], IB_out);
  xnor xnor_6 (xnor_6_out, b[5], IB_out);
  xnor xnor_7 (xnor_7_out, b[6], IB_out);
  xnor xnor_8 (xnor_8_out, b[7], IB_out);
  and XOR (XOR_out, opcode[3], not_3_out, op, not_2_out, not_1_out);
  and and_5 (and_5_out, nand_8_out, x1_out, xnor_1_out);
  nor nor_1 (nor_1_out, nand_8_out, OR_3_out, xnor_1_out);
  and and_6 (and_6_out, nand_1_out, x1_out, xnor_2_out);
  nor nor_2 (nor_2_out, nand_1_out, OR_3_out, xnor_2_out);
  and and_7 (and_7_out, nand_2_out, x1_out, xnor_3_out);
  nor nor_3 (nor_3_out, nand_2_out, OR_3_out, xnor_3_out);
  and and_8 (and_8_out, nand_3_out, x1_out, xnor_4_out);
  nor nor_4 (nor_4_out, nand_3_out, OR_3_out, xnor_4_out);
  and and_9 (and_9_out, nand_4_out, x1_out, xnor_5_out);
  nor nor_5 (nor_5_out, nand_4_out, OR_3_out, xnor_5_out);
  and and_10 (and_10_out, nand_5_out, x1_out, xnor_6_out);
  nor nor_6 (nor_6_out, nand_5_out, OR_3_out, xnor_6_out);
  and and_11 (and_11_out, nand_6_out, x1_out, xnor_7_out);
  nor nor_7 (nor_7_out, nand_6_out, OR_3_out, xnor_7_out);
  and and_12 (and_12_out, nand_7_out, x1_out, xnor_8_out);
  nor nor_8 (nor_8_out, nand_7_out, OR_3_out, xnor_8_out);
  and LSL (LSL_out, opcode[3], not_3_out, op, not_2_out, opcode[0]);
  or SL (shift_left, LSL_out, RCL_out, ROL_out);
  nor nor_9 (nor_9_out, and_5_out, nor_1_out);
  nor nor_10 (nor_10_out, and_6_out, nor_2_out);
  nor nor_11 (nor_11_out, and_7_out, nor_3_out);
  nor nor_12 (nor_12_out, and_8_out, nor_4_out);
  nor nor_13 (nor_13_out, and_9_out, nor_5_out);
  nor nor_14 (nor_14_out, and_10_out, nor_6_out);
  nor nor_15 (nor_15_out, and_11_out, nor_7_out);
  nor nor_16 (nor_16_out, and_12_out, nor_8_out);
  and LSR (LSR_out, opcode[3], not_3_out, op, opcode[1], not_1_out);
  and ASR (ASR_out, opcode[3], not_3_out, op, opcode[1], opcode[0]);
  or SR (shift_right, ASR_out, LSR_out, ROR_out, RCR_out);
  and ROL (ROL_out, opcode[3], opcode[2], op, not_2_out, not_1_out);
  or NS (NS_out, shift_left, shift_right);
  and and_13 (and_13_out, or_2_out, nor_9_out);
  xor xor_2 (xor_2_out, or_4_out, nor_10_out);
  and and_14 (and_14_out, or_2_out, nor_9_out, nor_10_out);
  and and_15 (and_15_out, nor_1_out, nor_10_out);
  xor xor_3 (xor_3_out, or_5_out, nor_11_out);
  and and_16 (and_16_out, or_2_out, nor_9_out, nor_10_out, nor_11_out);
  and and_17 (and_17_out, nor_1_out, nor_10_out, nor_11_out);
  and and_18 (and_18_out, nor_2_out, nor_11_out);
  and and_19 (and_19_out, or_2_out, nor_9_out, nor_10_out, nor_11_out, nor_12_out);
  and and_20 (and_20_out, nor_1_out, nor_10_out, nor_11_out, nor_12_out);
  and and_21 (and_21_out, nor_2_out, nor_11_out, nor_12_out);
  and and_22 (and_22_out, nor_3_out, nor_12_out);
  and and_23 (and_23_out, or_7_out, nor_13_out);
  and and_24 (and_24_out, or_7_out, nor_13_out, nor_14_out);
  and and_25 (and_25_out, nor_5_out, nor_14_out);
  and and_26 (and_26_out, or_7_out, nor_13_out, nor_14_out, nor_15_out);
  and and_27 (and_27_out, nor_5_out, nor_14_out, nor_15_out);
  and and_28 (and_28_out, nor_6_out, nor_15_out);
  and and_29 (and_29_out, or_7_out, nor_13_out, nor_14_out, nor_15_out, nor_16_out);
  and and_30 (and_30_out, nor_5_out, nor_14_out, nor_15_out, nor_16_out);
  and and_31 (and_31_out, nor_6_out, nor_15_out, nor_16_out);
  and and_32 (and_32_out, nor_16_out, nor_7_out);
  and ROR (ROR_out, opcode[3], opcode[2], op, not_2_out, opcode[0]);
  not not_5 (not_5_out, NS_out);
  xor xor_4 (xor_4_out, or_2_out, nor_9_out);
  or or_4 (or_4_out, and_13_out, XOR_out, nor_1_out);
  or or_5 (or_5_out, XOR_out, and_14_out, and_15_out, nor_2_out);
  or or_6 (or_6_out, and_16_out, and_17_out, XOR_out, and_18_out, nor_3_out);
  xor xor_5 (xor_5_out, or_6_out, nor_12_out);
  or or_7 (or_7_out, XOR_out, and_19_out, and_20_out, and_22_out, nor_4_out, and_21_out);
  or or_8 (or_8_out, and_23_out, XOR_out, nor_5_out);
  or or_9 (or_9_out, XOR_out, and_24_out, nor_6_out, and_25_out);
  or or_10 (or_10_out, and_26_out, and_27_out, XOR_out, and_28_out, nor_7_out);
  and RCL (RCL_out, opcode[3], opcode[2], op, opcode[1], not_1_out);
  or or_11 (or_11_out, XOR_out, and_29_out, and_30_out, and_32_out, nor_8_out, and_31_out);
  and RCR (RCR_out, opcode[3], opcode[2], op, opcode[1], opcode[0]);
  and and_33 (and_33_out, not_5_out, xor_4_out);
  or or_12 (or_12_out, and_33_out, and_34_out, and_35_out);
  and and_34 (and_34_out, shift_left, or_2_out);
  and and_35 (and_35_out, shift_right, b[1]);
  and and_36 (and_36_out, not_5_out, xor_2_out);
  and and_37 (and_37_out, shift_left, b[0]);
  and and_38 (and_38_out, shift_right, b[2]);
  and and_39 (and_39_out, not_5_out, xor_3_out);
  and and_40 (and_40_out, shift_left, b[1]);
  and and_41 (and_41_out, shift_right, b[3]);
  and and_42 (and_42_out, not_5_out, xor_5_out);
  and and_43 (and_43_out, shift_left, b[2]);
  and and_44 (and_44_out, shift_right, b[4]);
  xor xor_6 (xor_6_out, or_7_out, nor_13_out);
  xor xor_7 (xor_7_out, or_8_out, nor_14_out);
  xor xor_8 (xor_8_out, or_9_out, nor_15_out);
  xor xor_9 (xor_9_out, or_10_out, nor_16_out);
  or or_13 (or_13_out, and_36_out, and_37_out, and_38_out);
  or or_14 (or_14_out, and_39_out, and_40_out, and_41_out);
  or or_15 (or_15_out, and_42_out, and_43_out, and_44_out);
  and and_45 (and_45_out, not_5_out, xor_6_out);
  and and_46 (and_46_out, shift_left, b[5]);
  and and_47 (and_47_out, shift_right, b[3]);
  and and_48 (and_48_out, not_5_out, xor_7_out);
  and and_49 (and_49_out, shift_left, b[4]);
  and and_50 (and_50_out, shift_right, b[6]);
  and and_51 (and_51_out, not_5_out, xor_8_out);
  and and_52 (and_52_out, shift_left, b[5]);
  and and_53 (and_53_out, shift_right, b[7]);
  and and_54 (and_54_out, not_5_out, xor_9_out);
  and and_55 (and_55_out, shift_left, b[6]);
  and and_56 (and_56_out, shift_right, or_2_out);
  xor xor_10 (overflow, or_10_out, or_11_out);
  or or_16 (or_16_out, and_45_out, and_46_out, and_47_out);
  or or_17 (or_17_out, and_48_out, and_49_out, and_50_out);
  or or_18 (or_18_out, and_51_out, and_52_out, and_53_out);
  or or_19 (\négatif , and_54_out, and_55_out, and_56_out);
  and and_57 (and_57_out, not_5_out, or_11_out);
  and and_58 (and_58_out, shift_left, b[7]);
  or or_20 (carry, and_57_out, and_58_out, and_59_out);
  and and_59 (and_59_out, shift_right, b[0]);
  nor nor_17 (zero, or_12_out, or_13_out, or_14_out, or_15_out, or_16_out, or_17_out, or_18_out, \négatif );
  nor nor_18 (nor_18_out, nor_58_out, input_enable);
  and and_60 (and_60_out, input_enable, or_12_out);
  nor nor_19 (nor_19_out, nor_60_out, input_enable);
  and and_61 (and_61_out, input_enable, or_13_out);
  nor nor_20 (nor_20_out, nor_62_out, input_enable);
  and and_62 (and_62_out, input_enable, or_14_out);
  nor nor_21 (nor_21_out, nor_64_out, input_enable);
  and and_63 (and_63_out, input_enable, or_15_out);
  nor nor_22 (nor_22_out, nor_66_out, input_enable);
  and and_64 (and_64_out, input_enable, or_16_out);
  nor nor_23 (nor_23_out, nor_68_out, input_enable);
  and and_65 (and_65_out, input_enable, or_17_out);
  nor nor_24 (nor_24_out, nor_70_out, input_enable);
  and and_66 (and_66_out, input_enable, or_18_out);
  nor nor_25 (nor_25_out, nor_72_out, input_enable);
  and and_67 (and_67_out, input_enable, \négatif );
  nor nor_26 (nor_26_out, nor_18_out, and_60_out, clock);
  nor nor_27 (nor_27_out, nor_26_out, clock);
  nor nor_28 (nor_28_out, nor_19_out, and_61_out, clock);
  nor nor_29 (nor_29_out, nor_28_out, clock);
  nor nor_30 (nor_30_out, nor_20_out, and_62_out, clock);
  nor nor_31 (nor_31_out, nor_30_out, clock);
  nor nor_32 (nor_32_out, nor_21_out, and_63_out, clock);
  nor nor_33 (nor_33_out, nor_32_out, clock);
  nor nor_34 (nor_34_out, nor_22_out, and_64_out, clock);
  nor nor_35 (nor_35_out, nor_34_out, clock);
  nor nor_36 (nor_36_out, nor_23_out, and_65_out, clock);
  nor nor_37 (nor_37_out, nor_36_out, clock);
  nor nor_38 (nor_38_out, nor_24_out, and_66_out, clock);
  nor nor_39 (nor_39_out, nor_38_out, clock);
  nor nor_40 (nor_40_out, nor_25_out, and_67_out, clock);
  nor nor_41 (nor_41_out, nor_40_out, clock);
  nor nor_42 (nor_42_out, nor_26_out, nor_43_out);
  nor nor_43 (nor_43_out, nor_42_out, nor_27_out);
  nor nor_44 (nor_44_out, nor_28_out, nor_45_out);
  nor nor_45 (nor_45_out, nor_44_out, nor_29_out);
  nor nor_46 (nor_46_out, nor_30_out, nor_47_out);
  nor nor_47 (nor_47_out, nor_46_out, nor_31_out);
  nor nor_48 (nor_48_out, nor_32_out, nor_49_out);
  nor nor_49 (nor_49_out, nor_48_out, nor_33_out);
  nor nor_50 (nor_50_out, nor_34_out, nor_51_out);
  nor nor_51 (nor_51_out, nor_50_out, nor_35_out);
  nor nor_52 (nor_52_out, nor_36_out, nor_53_out);
  nor nor_53 (nor_53_out, nor_52_out, nor_37_out);
  nor nor_54 (nor_54_out, nor_38_out, nor_55_out);
  nor nor_55 (nor_55_out, nor_54_out, nor_39_out);
  nor nor_56 (nor_56_out, nor_40_out, nor_57_out);
  nor nor_57 (nor_57_out, nor_56_out, nor_41_out);
  nor nor_58 (nor_58_out, and_68_out, out_9);
  and and_68 (and_68_out, nor_42_out, clock);
  nor nor_59 (out_9, nor_58_out, and_69_out);
  and and_69 (and_69_out, clock, nor_43_out);
  nor nor_60 (nor_60_out, and_70_out, out_10);
  and and_70 (and_70_out, nor_44_out, clock);
  nor nor_61 (out_10, nor_60_out, and_71_out);
  and and_71 (and_71_out, clock, nor_45_out);
  nor nor_62 (nor_62_out, and_72_out, out_11);
  and and_72 (and_72_out, nor_46_out, clock);
  and and_73 (and_73_out, clock, nor_47_out);
  nor nor_63 (out_11, nor_62_out, and_73_out);
  nor nor_64 (nor_64_out, and_74_out, out_12);
  and and_74 (and_74_out, nor_48_out, clock);
  and and_75 (and_75_out, clock, nor_49_out);
  nor nor_65 (out_12, nor_64_out, and_75_out);
  nor nor_66 (nor_66_out, and_76_out, out_13);
  and and_76 (and_76_out, nor_50_out, clock);
  and and_77 (and_77_out, clock, nor_51_out);
  nor nor_67 (out_13, nor_66_out, and_77_out);
  nor nor_68 (nor_68_out, and_78_out, out_14);
  and and_78 (and_78_out, nor_52_out, clock);
  and and_79 (and_79_out, clock, nor_53_out);
  nor nor_69 (out_14, nor_68_out, and_79_out);
  nor nor_70 (nor_70_out, and_80_out, out_16);
  and and_80 (and_80_out, nor_54_out, clock);
  and and_81 (and_81_out, clock, nor_55_out);
  nor nor_71 (out_16, nor_70_out, and_81_out);
  nor nor_72 (nor_72_out, and_82_out, out_17);
  and and_82 (and_82_out, nor_56_out, clock);
  and and_83 (and_83_out, clock, nor_57_out);
  nor nor_73 (out_17, nor_72_out, and_83_out);

  // Notes on the sheet:
  //   x2
  //   x3
endmodule

module sequentiel (
  input  latch_is_on,
  input  reset,
  input  latch_is_on_2,
  input  reset_2,
  input  clock,
  input  input_enable,
  input  data,
  output out_8,
  output out_9,
  output out_10,
  output out_11,
  output out_12,
  output out_13,
  output out_14,
  output out_15
);

  wire and_1_out, and_2_out, and_3_out, and_4_out, and_5_out, nand_1_out, nand_2_out, nand_5_out, nand_6_out,
       nor_3_out, nor_4_out, nor_5_out, nor_6_out, nor_7_out, not_1_out, not_2_out, not_3_out;

  not not_1 (not_1_out, reset);
  and and_1 (and_1_out, not_1_out, latch_is_on);
  not not_2 (not_2_out, and_1_out);
  and and_2 (and_2_out, not_2_out, latch_is_on);
  not not_3 (not_3_out, latch_is_on_2);
  and and_3 (and_3_out, input_enable, data);
  nor nor_1 (out_8, and_1_out, out_9);
  nor nor_2 (out_9, out_8, and_2_out);
  nand nand_1 (nand_1_out, reset_2, not_3_out);
  nand nand_2 (nand_2_out, nand_1_out, not_3_out);
  nor nor_3 (nor_3_out, out_14, input_enable);
  nor nor_4 (nor_4_out, nor_3_out, and_3_out, clock);
  nor nor_5 (nor_5_out, nor_4_out, clock);
  nand nand_3 (out_10, nand_1_out, out_12);
  nand nand_4 (out_12, out_10, nand_2_out);
  nor nor_6 (nor_6_out, nor_4_out, nor_7_out);
  nor nor_7 (nor_7_out, nor_6_out, nor_5_out);
  and and_4 (and_4_out, nor_6_out, clock);
  and and_5 (and_5_out, clock, nor_7_out);
  nor nor_8 (out_14, and_4_out, out_15);
  nor nor_9 (out_15, out_14, and_5_out);
  nand nand_5 (nand_5_out, out_10, latch_is_on_2);
  nand nand_6 (nand_6_out, nand_5_out, latch_is_on_2);
  nand nand_7 (out_11, nand_5_out, out_13);
  nand nand_8 (out_13, out_11, nand_6_out);
endmodule
