// Logisim project full_adder_4bits_carry_lkhd.circ as structural Verilog: 1 circuit, main circuit full_adder_4bits_carry_lkhd
module full_adder_4bits_carry_lkhd (
  input  minus,
  input  [7:0] a,
  input  [7:0] b,
  output [7:0] out_4,
  output overflow
);

  wire and_1_out, and_2_out, and_3_out, and_4_out, and_5_out, and_6_out, and_7_out, and_8_out, and_9_out,
       and_10_out, and_11_out, and_12_out, and_13_out, and_14_out, and_15_out, and_16_out, and_17_out,
       and_18_out, and_19_out, and_20_out, and_21_out, and_22_out, and_23_out, and_24_out, and_25_out,
       and_26_out, and_27_out, and_28_out, and_29_out, or_1_out, or_2_out, or_3_out, or_4_out, or_5_out,
       or_6_out, or_7_out, or_9_out, xor_1_out, xor_2_out, xor_3_out, xor_4_out, xor_5_out, xor_6_out,
       xor_7_out, xor_8_out, xor_9_out, xor_10_out, xor_11_out, xor_12_out, xor_13_out, xor_14_out,
       xor_15_out, xor_16_out;

  xor xor_1 (xor_1_out, b[0], minus);
  xor xor_2 (xor_2_out, b[1], minus);
  xor xor_3 (xor_3_out, b[2], minus);
  xor xor_4 (xor_4_out, b[3], minus);
  xor xor_5 (xor_5_out, b[4], minus);
  xor xor_6 (xor_6_out, b[5], minus);
  xor xor_7 (xor_7_out, b[6], minus);
  xor xor_8 (xor_8_out, a[0], xor_1_out);
  and and_1 (and_1_out, xor_1_out, a[0]);
  xor xor_9 (xor_9_out, a[1], xor_2_out);
  and and_2 (and_2_out, xor_2_out, a[1]);
  xor xor_10 (xor_10_out, a[2], xor_3_out);
  and and_3 (and_3_out, xor_3_out, a[2]);
  xor xor_11 (xor_11_out, a[3], xor_4_out);
  and and_4 (and_4_out, xor_4_out, a[3]);
  xor xor_12 (xor_12_out, a[4], xor_5_out);
  and and_5 (and_5_out, xor_5_out, a[4]);
  xor xor_13 (xor_13_out, a[5], xor_6_out);
  and and_6 (and_6_out, xor_6_out, a[5]);
  xor xor_14 (xor_14_out, a[6], xor_7_out);
  and and_7 (and_7_out, xor_7_out, a[6]);
  xor xor_15 (xor_15_out, a[7], xor_16_out);
  xor xor_16 (xor_16_out, b[7], minus);
  and and_8 (and_8_out, xor_16_out, a[7]);
  xor xor_17 (out_4[0], minus, xor_8_out);
  xor xor_18 (out_4[1], or_1_out, xor_9_out);
  xor xor_19 (out_4[2], or_2_out, xor_10_out);
  xor xor_20 (out_4[3], or_3_out, xor_11_out);
  xor xor_21 (out_4[4], or_9_out, xor_12_out);
  xor xor_22 (out_4[5], or_5_out, xor_13_out);
  xor xor_23 (out_4[6], or_6_out, xor_14_out);
  xor xor_24 (out_4[7], or_7_out, xor_15_out);
  and and_9 (and_9_out, minus, xor_8_out);
  or or_1 (or_1_out, and_9_out, and_1_out);
  and and_10 (and_10_out, minus, xor_8_out, xor_9_out);
  and and_11 (and_11_out, and_1_out, xor_9_out);
  or or_2 (or_2_out, and_10_out, and_11_out, and_2_out);
  and and_12 (and_12_out, minus, xor_8_out, xor_9_out, xor_10_out);
  and and_13 (and_13_out, and_1_out, xor_9_out, xor_10_out);
  or or_3 (or_3_out, and_12_out, and_13_out, and_14_out, and_3_out);
  and and_14 (and_14_out, and_2_out, xor_10_out);
  and and_15 (and_15_out, minus, xor_8_out, xor_9_out, xor_10_out, xor_11_out);
  and and_16 (and_16_out, and_1_out, xor_9_out, xor_10_out, xor_11_out);
  and and_17 (and_17_out, and_2_out, xor_10_out, xor_11_out);
  and and_18 (and_18_out, and_3_out, xor_11_out);
  and and_19 (and_19_out, or_9_out, xor_12_out);
  and and_20 (and_20_out, or_9_out, xor_12_out, xor_13_out);
  and and_21 (and_21_out, and_5_out, xor_13_out);
  and and_22 (and_22_out, or_9_out, xor_12_out, xor_13_out, xor_14_out);
  and and_23 (and_23_out, and_5_out, xor_13_out, xor_14_out);
  and and_24 (and_24_out, and_6_out, xor_14_out);
  and and_25 (and_25_out, or_9_out, xor_12_out, xor_13_out, xor_14_out, xor_15_out);
  and and_26 (and_26_out, and_5_out, xor_13_out, xor_14_out, xor_15_out);
  and and_27 (and_27_out, and_6_out, xor_14_out, xor_15_out);
  and and_28 (and_28_out, and_7_out, xor_15_out);
  and and_29 (and_29_out, minus, or_4_out);
  or or_4 (or_4_out, and_15_out, and_16_out, and_17_out, and_18_out, and_4_out);
  or or_5 (or_5_out, and_19_out, and_5_out);
  or or_6 (or_6_out, and_20_out, and_21_out, and_6_out);
  or or_7 (or_7_out, and_22_out, and_23_out, and_24_out, and_7_out);
  or or_8 (overflow, and_25_out, and_26_out, and_27_out, and_28_out, and_8_out);
  or or_9 (or_9_out, and_15_out, and_29_out);
endmodule
